// Logisim project jrmips.circ as structural Verilog: 9 circuits, main circuit main
module main (
);

  wire Clock_out, Comparator_output, Control_alusrc, Control_branch, Control_halt, Control_jumpimmed,
       Control_jumpreg, Control_memwrite, Control_mul_div, Control_regwrite, Control_setdisplay,
       Instr_Dcdr_subop, not_1_out, or_1_out;
  wire [2:0] Control_writesource0, Instr_Dcdr_rs, Instr_Dcdr_rt;
  wire [3:0] Instr_Dcdr_opcode;
  wire [7:0] adder_1_out, Instr_Dcdr_immed, multiplexer_1_out, multiplexer_2_out, PC_q;
  wire [15:0] ALU_aluout, bit_extender_1_out, bit_extender_2_out, bit_extender_3_out, DigitRegister_q,
       divider_1_out, divider_1_rem, multiplexer_3_out, multiplexer_4_out, multiplexer_5_out,
       multiplexer_6_out, multiplier_1_cout, multiplier_1_out, ram_1_data, RegFile_read_data_1__rs,
       RegFile_read_data_2__rt, rom_1_data, Shifter_output;

  Multiplexer #(.width(8)) multiplexer_1 (
    .in0(multiplexer_2_out), .in1(RegFile_read_data_1__rs[7:0]), .out(multiplexer_1_out),
    .sel(Control_jumpreg));  // open: en
  Multiplexer #(.width(8)) multiplexer_2 (
    .in0(adder_1_out), .in1(Instr_Dcdr_immed), .out(multiplexer_2_out), .sel(or_1_out));  // open: en
  or or_1 (or_1_out, Control_jumpimmed, Comparator_output);
  Register PC (.D(multiplexer_1_out), .en(not_1_out), .Q(PC_q), .clk(Clock_out));  // open: clr
  not not_1 (not_1_out, Control_halt);
  Clock Clock (.out(Clock_out));
  branch_comparator Comparator (
    .Opcode1(Instr_Dcdr_opcode[1]), .Opcode0(Instr_Dcdr_opcode[0]), .Subop(Instr_Dcdr_subop),
    .branch(Control_branch), .rs(RegFile_read_data_1__rs), .\output (Comparator_output));
  LED Halt_LED (.in(Control_halt));
  Instr_Decoder Instr_Dcdr (
    .Instruction(rom_1_data), .Subop(Instr_Dcdr_subop), .Immed(Instr_Dcdr_immed), .rt(Instr_Dcdr_rt),
    .rs(Instr_Dcdr_rs), .Opcode(Instr_Dcdr_opcode));
  ROM #(.dataWidth(16)) rom_1 (.addr(PC_q), .data(rom_1_data));  // open: sel
  Control Control (
    .Opcode3(Instr_Dcdr_opcode[3]), .MemWrite(Control_memwrite), .Opcode2(Instr_Dcdr_opcode[2]),
    .Opcode1(Instr_Dcdr_opcode[1]), .Opcode0(Instr_Dcdr_opcode[0]), .JumpImmed(Control_jumpimmed),
    .Subop(Instr_Dcdr_subop), .Mul_Div(Control_mul_div), .branch(Control_branch),
    .WriteSource_2(Control_writesource0[2]), .WriteSource_1(Control_writesource0[1]),
    .WriteSource0(Control_writesource0[0]), .RegWrite(Control_regwrite), .SetDisplay(Control_setdisplay),
    .Halt(Control_halt), .ALUsrc(Control_alusrc), .JumpReg(Control_jumpreg));
  Adder adder_1 (.a(8'h1), .b(PC_q), .out(adder_1_out));  // open: cin, cout
  RegFile RegFile (
    .WriteData1(multiplexer_4_out), .WriteRegister1(Instr_Dcdr_rs), .WriteEnable(Control_regwrite),
    .Read_Data_1__rs(RegFile_read_data_1__rs), .Read_Data_2__rt(RegFile_read_data_2__rt),
    .ReadRegister1(Instr_Dcdr_rs), .ReadRegister2(Instr_Dcdr_rt), .Clock(Clock_out),
    .mul_div(Control_mul_div), .WriteData2(multiplexer_6_out));
  assign bit_extender_1_out = {{8{Instr_Dcdr_immed[7]}}, Instr_Dcdr_immed};  // Bit_Extender bit_extender_1
  assign bit_extender_2_out = {{8{1'b0}}, Instr_Dcdr_immed};  // Bit_Extender bit_extender_2
  Multiplexer #(.width(16)) multiplexer_3 (
    .in0(bit_extender_1_out), .in1(bit_extender_2_out), .out(multiplexer_3_out), .sel(Instr_Dcdr_subop));  // open: en
  Register #(.width(16)) DigitRegister (
    .D(RegFile_read_data_1__rs), .en(Control_setdisplay), .Q(DigitRegister_q), .clk(Clock_out));  // open: clr
  Multiplexer #(.select(3), .width(16)) multiplexer_4 (
    .in0(bit_extender_2_out), .in1(ALU_aluout), .in2(divider_1_out), .in3(multiplier_1_out),
    .in4(Shifter_output), .in5(ram_1_data), .in6(bit_extender_3_out), .out(multiplexer_4_out),
    .sel(Control_writesource0));  // open: in7, en
  Multiplexer #(.width(16)) multiplexer_5 (
    .in0(RegFile_read_data_2__rt), .in1(multiplexer_3_out), .out(multiplexer_5_out), .sel(Control_alusrc));  // open: en
  Multiplexer #(.width(16)) multiplexer_6 (
    .in0(divider_1_rem), .in1(multiplier_1_cout), .out(multiplexer_6_out), .sel(Instr_Dcdr_subop));  // open: en
  Hex_Digit_Display hex_digit_display_1 (.value(DigitRegister_q[15:12]));  // open: dp
  assign bit_extender_3_out = {{8{1'b0}}, adder_1_out};  // Bit_Extender bit_extender_3
  ALU ALU (
    .Opcode(Instr_Dcdr_opcode), .Input_A(RegFile_read_data_1__rs), .Input_B(multiplexer_5_out),
    .Subop(Instr_Dcdr_subop), .ALUout(ALU_aluout));
  Shifter Shifter (
    .ValToShift(RegFile_read_data_1__rs), .ShiftAmt(multiplexer_5_out), .Output(Shifter_output),
    .Subop(Instr_Dcdr_subop));
  Divider #(.width(16)) divider_1 (
    .a(RegFile_read_data_1__rs), .b(multiplexer_5_out), .out(divider_1_out), .rem(divider_1_rem));  // open: upper
  Multiplier #(.width(16)) multiplier_1 (
    .a(RegFile_read_data_1__rs), .b(multiplexer_5_out), .out(multiplier_1_out), .cout(multiplier_1_cout));  // open: cin
  Hex_Digit_Display hex_digit_display_2 (.value(DigitRegister_q[11:8]));  // open: dp
  Hex_Digit_Display hex_digit_display_3 (.value(DigitRegister_q[7:4]));  // open: dp
  Hex_Digit_Display hex_digit_display_4 (.value(DigitRegister_q[3:0]));  // open: dp
  RAM #(.dataWidth(16), .bus("separate")) ram_1 (
    .addr(RegFile_read_data_2__rt[7:0]), .din(RegFile_read_data_1__rs), .data(ram_1_data),
    .str(Control_memwrite), .clk(Clock_out));  // open: sel, ld, clr

  // Notes on the sheet:
  //   Andrew Puglionesi
  //   aop4@pitt.edu
  //   Instr mem
  //   contents of rom_1 (hex, n*v repeats v):
  //   8028 b000 8202 2040 b000 8000 5001
endmodule

module RegFile (
  input  mul_div,
  input  [2:0] ReadRegister1,
  input  [15:0] WriteData1,
  input  [2:0] WriteRegister1,
  input  [2:0] ReadRegister2,
  input  WriteEnable,
  input  [15:0] WriteData2,
  input  Clock,
  output [15:0] Read_Data_1__rs,
  output [15:0] Read_Data_2__rt
);

  wire and_1_out, decoder_1_out0, decoder_1_out1, decoder_1_out2, decoder_1_out3, decoder_1_out4,
       decoder_1_out5, decoder_1_out6, decoder_1_out7, littleandgate_1_output, littleandgate_2_output,
       littleandgate_3_output, littleandgate_4_output, littleandgate_5_output, littleandgate_6_output,
       littleandgate_7_output, littleandgate_8_output, or_1_out, or_2_out, or_3_out, or_4_out, or_5_out,
       or_6_out, or_7_out, or_8_out;
  wire [2:0] adder_1_out;
  wire [15:0] _0_q, _1_q, _2_q, _3_q, _4_q, _5_q, _6_q, _7_q, demultiplexer_1_out0, demultiplexer_1_out1,
       demultiplexer_1_out2, demultiplexer_1_out3, demultiplexer_1_out4, demultiplexer_1_out5,
       demultiplexer_1_out6, demultiplexer_1_out7, demultiplexer_2_out0, demultiplexer_2_out1,
       demultiplexer_2_out2, demultiplexer_2_out3, demultiplexer_2_out4, demultiplexer_2_out5,
       demultiplexer_2_out6, demultiplexer_2_out7, multiplexer_1_out, multiplexer_2_out, multiplexer_3_out,
       multiplexer_4_out, multiplexer_5_out, multiplexer_6_out, multiplexer_7_out, multiplexer_8_out;

  Demultiplexer #(.select(3), .width(16)) demultiplexer_1 (
    .out0(demultiplexer_1_out0), .out1(demultiplexer_1_out1), .out2(demultiplexer_1_out2),
    .out3(demultiplexer_1_out3), .out4(demultiplexer_1_out4), .out5(demultiplexer_1_out5),
    .out6(demultiplexer_1_out6), .out7(demultiplexer_1_out7), .in(WriteData1), .sel(WriteRegister1),
    .en(WriteEnable));
  Demultiplexer #(.select(3), .width(16)) demultiplexer_2 (
    .out0(demultiplexer_2_out0), .out1(demultiplexer_2_out1), .out2(demultiplexer_2_out2),
    .out3(demultiplexer_2_out3), .out4(demultiplexer_2_out4), .out5(demultiplexer_2_out5),
    .out6(demultiplexer_2_out6), .out7(demultiplexer_2_out7), .in(WriteData2), .sel(adder_1_out),
    .en(and_1_out));
  and and_1 (and_1_out, WriteEnable, mul_div);
  Decoder #(.select(3)) decoder_1 (
    .out0(decoder_1_out0), .out1(decoder_1_out1), .out2(decoder_1_out2), .out3(decoder_1_out3),
    .out4(decoder_1_out4), .out5(decoder_1_out5), .out6(decoder_1_out6), .out7(decoder_1_out7),
    .sel(WriteRegister1));  // open: en
  Adder #(.width(3)) adder_1 (.a(WriteRegister1), .b(3'b001), .out(adder_1_out));  // open: cin, cout
  Multiplexer #(.width(16)) multiplexer_1 (
    .in0(demultiplexer_1_out0), .in1(demultiplexer_2_out0), .out(multiplexer_1_out), .sel(decoder_1_out7));  // open: en
  Multiplexer #(.width(16)) multiplexer_2 (
    .in0(demultiplexer_1_out1), .in1(demultiplexer_2_out1), .out(multiplexer_2_out), .sel(decoder_1_out0));  // open: en
  Multiplexer #(.width(16)) multiplexer_3 (
    .in0(demultiplexer_1_out2), .in1(demultiplexer_2_out2), .out(multiplexer_3_out), .sel(decoder_1_out1));  // open: en
  Multiplexer #(.width(16)) multiplexer_4 (
    .in0(demultiplexer_1_out3), .in1(demultiplexer_2_out3), .out(multiplexer_4_out), .sel(decoder_1_out2));  // open: en
  Multiplexer #(.width(16)) multiplexer_5 (
    .in0(demultiplexer_1_out4), .in1(demultiplexer_2_out4), .out(multiplexer_5_out), .sel(decoder_1_out3));  // open: en
  Multiplexer #(.width(16)) multiplexer_6 (
    .in0(demultiplexer_1_out5), .in1(demultiplexer_2_out5), .out(multiplexer_6_out), .sel(decoder_1_out4));  // open: en
  Multiplexer #(.width(16)) multiplexer_7 (
    .in0(demultiplexer_1_out6), .in1(demultiplexer_2_out6), .out(multiplexer_7_out), .sel(decoder_1_out5));  // open: en
  Multiplexer #(.width(16)) multiplexer_8 (
    .in0(demultiplexer_1_out7), .in1(demultiplexer_2_out7), .out(multiplexer_8_out), .sel(decoder_1_out6));  // open: en
  LittleAndGate littleandgate_1 (.input1(decoder_1_out7), .input2(mul_div), .\output (littleandgate_1_output));
  LittleAndGate littleandgate_2 (.input1(mul_div), .input2(decoder_1_out0), .\output (littleandgate_2_output));
  LittleAndGate littleandgate_3 (.input1(mul_div), .input2(decoder_1_out1), .\output (littleandgate_3_output));
  LittleAndGate littleandgate_4 (.input1(mul_div), .input2(decoder_1_out2), .\output (littleandgate_4_output));
  LittleAndGate littleandgate_5 (.input1(mul_div), .input2(decoder_1_out3), .\output (littleandgate_5_output));
  LittleAndGate littleandgate_6 (.input1(mul_div), .input2(decoder_1_out4), .\output (littleandgate_6_output));
  LittleAndGate littleandgate_7 (.input1(mul_div), .input2(decoder_1_out5), .\output (littleandgate_7_output));
  LittleAndGate littleandgate_8 (.input1(mul_div), .input2(decoder_1_out6), .\output (littleandgate_8_output));
  Register #(.width(16)) _0 (.D(multiplexer_1_out), .en(or_1_out), .Q(_0_q), .clk(Clock));  // open: clr
  or or_1 (or_1_out, littleandgate_1_output, decoder_1_out0);
  Register #(.width(16)) _1 (.D(multiplexer_2_out), .en(or_2_out), .Q(_1_q), .clk(Clock));  // open: clr
  or or_2 (or_2_out, decoder_1_out1, littleandgate_2_output);
  Register #(.width(16)) _2 (.D(multiplexer_3_out), .en(or_3_out), .Q(_2_q), .clk(Clock));  // open: clr
  or or_3 (or_3_out, decoder_1_out2, littleandgate_3_output);
  Register #(.width(16)) _3 (.D(multiplexer_4_out), .en(or_4_out), .Q(_3_q), .clk(Clock));  // open: clr
  or or_4 (or_4_out, decoder_1_out3, littleandgate_4_output);
  Register #(.width(16)) _4 (.D(multiplexer_5_out), .en(or_5_out), .Q(_4_q), .clk(Clock));  // open: clr
  or or_5 (or_5_out, decoder_1_out4, littleandgate_5_output);
  Register #(.width(16)) _5 (.D(multiplexer_6_out), .en(or_6_out), .Q(_5_q), .clk(Clock));  // open: clr
  or or_6 (or_6_out, decoder_1_out5, littleandgate_6_output);
  Register #(.width(16)) _6 (.D(multiplexer_7_out), .en(or_7_out), .Q(_6_q), .clk(Clock));  // open: clr
  or or_7 (or_7_out, decoder_1_out6, littleandgate_7_output);
  Register #(.width(16)) _7 (.D(multiplexer_8_out), .en(or_8_out), .Q(_7_q), .clk(Clock));  // open: clr
  or or_8 (or_8_out, decoder_1_out7, littleandgate_8_output);
  Multiplexer #(.select(3), .width(16)) multiplexer_9 (
    .in0(_0_q), .in1(_1_q), .in2(_2_q), .in3(_3_q), .in4(_4_q), .in5(_5_q), .in6(_6_q), .in7(_7_q),
    .out(Read_Data_1__rs), .sel(ReadRegister1));  // open: en
  Multiplexer #(.select(3), .width(16)) multiplexer_10 (
    .in0(_0_q), .in1(_1_q), .in2(_2_q), .in3(_3_q), .in4(_4_q), .in5(_5_q), .in6(_6_q), .in7(_7_q),
    .out(Read_Data_2__rt), .sel(ReadRegister2));  // open: en
endmodule

module ALU (
  input  [3:0] Opcode,
  input  [15:0] Input_A,
  input  [15:0] Input_B,
  input  Subop,
  output [15:0] ALUout
);

  wire and_2_out, nor_1_out, not_2_out;
  wire [15:0] adder_1_out, and_1_out, multiplexer_1_out, multiplexer_2_out, not_1_out, or_1_out,
       subtractor_1_out;

  Adder #(.width(16)) adder_1 (.a(Input_A), .b(Input_B), .out(adder_1_out));  // open: cin, cout
  Subtractor #(.width(16)) subtractor_1 (.a(Input_A), .b(Input_B), .out(subtractor_1_out));  // open: bin, bout
  assign and_1_out = Input_A & Input_B;  // AND_Gate and_1, 16 bits wide
  assign or_1_out = Input_B | Input_A;  // OR_Gate or_1, 16 bits wide
  assign not_1_out = ~or_1_out;  // NOT_Gate not_1, 16 bits wide
  Multiplexer #(.width(16)) multiplexer_1 (
    .in0(adder_1_out), .in1(subtractor_1_out), .out(multiplexer_1_out), .sel(and_2_out));  // open: en
  and and_2 (and_2_out, Subop, not_2_out);
  Multiplexer #(.width(16)) multiplexer_2 (
    .in0(and_1_out), .in1(not_1_out), .out(multiplexer_2_out), .sel(Subop));  // open: en
  not not_2 (not_2_out, Opcode[0]);
  nor nor_1 (nor_1_out, Opcode[0], Opcode[1]);
  Multiplexer #(.width(16)) multiplexer_3 (
    .in0(multiplexer_1_out), .in1(multiplexer_2_out), .out(ALUout), .sel(nor_1_out));  // open: en
endmodule

module Shifter (
  input  [15:0] ValToShift,
  input  [15:0] ShiftAmt,
  input  Subop,
  output [15:0] Output
);

  wire [3:0] bitselector_1_out;
  wire [15:0] shifter_1_out, shifter_2_out;

  BitSelector #(.width(16), .group(4)) bitselector_1 (.in(ShiftAmt), .out(bitselector_1_out), .sel(2'b00));
  Shifter_part #(.width(16)) shifter_1 (.in(ValToShift), .\dist (bitselector_1_out), .out(shifter_1_out));
  Shifter_part #(.width(16), .shift("lr")) shifter_2 (.in(ValToShift), .\dist (bitselector_1_out), .out(shifter_2_out));
  Multiplexer #(.width(16)) multiplexer_1 (
    .in0(shifter_1_out), .in1(shifter_2_out), .out(Output), .sel(Subop));  // open: en
endmodule

module Instr_Decoder (
  input  [15:0] Instruction,
  output Subop,
  output [7:0] Immed,
  output [2:0] rt,
  output [2:0] rs,
  output [3:0] Opcode
);


  assign Immed = Instruction[8:1];
  assign Opcode = Instruction[15:12];
  assign rs = Instruction[11:9];
  assign rt = Instruction[8:6];
  assign Subop = Instruction[0];
endmodule

module Control (
  input  Opcode3,
  input  Opcode2,
  input  Opcode1,
  input  Opcode0,
  input  Subop,
  output MemWrite,
  output JumpImmed,
  output Mul_Div,
  output branch,
  output WriteSource_2,
  output WriteSource_1,
  output WriteSource0,
  output RegWrite,
  output SetDisplay,
  output Halt,
  output ALUsrc,
  output JumpReg
);

  wire and_2_out, and_3_out, and_5_out, and_6_out, and_7_out, and_8_out, and_9_out, and_10_out, and_11_out,
       and_12_out, and_13_out, and_14_out, and_15_out, and_16_out, and_17_out, and_18_out, and_19_out,
       and_20_out, not_1_out, not_2_out, not_3_out, not_4_out, not_5_out, not_6_out, not_7_out, not_8_out,
       not_9_out, not_10_out, not_11_out, not_12_out, not_13_out, not_14_out, not_15_out, not_16_out,
       not_17_out, not_18_out, not_19_out, not_20_out, not_21_out, not_22_out, not_23_out, not_24_out,
       not_25_out, not_26_out, not_27_out, not_28_out, not_29_out, not_30_out, not_31_out, not_32_out,
       not_33_out, not_34_out, not_35_out, not_36_out, not_37_out, not_38_out, not_39_out, not_40_out,
       not_41_out, not_42_out, not_43_out, not_44_out, not_45_out;

  not not_1 (not_1_out, Opcode3);
  not not_2 (not_2_out, Opcode2);
  not not_3 (not_3_out, Opcode1);
  not not_4 (not_4_out, Subop);
  not not_5 (not_5_out, Opcode2);
  not not_6 (not_6_out, Opcode0);
  not not_7 (not_7_out, Opcode3);
  not not_8 (not_8_out, Opcode2);
  not not_9 (not_9_out, Opcode3);
  not not_10 (not_10_out, Opcode1);
  not not_11 (not_11_out, Opcode3);
  not not_12 (not_12_out, Opcode0);
  not not_13 (not_13_out, Opcode1);
  not not_14 (not_14_out, Subop);
  not not_15 (not_15_out, Opcode2);
  not not_16 (not_16_out, Opcode3);
  not not_17 (not_17_out, Opcode2);
  not not_18 (not_18_out, Subop);
  not not_19 (not_19_out, Opcode3);
  not not_20 (not_20_out, Opcode2);
  not not_21 (not_21_out, Opcode1);
  not not_22 (not_22_out, Opcode3);
  not not_23 (not_23_out, Opcode1);
  not not_24 (not_24_out, Opcode0);
  not not_25 (not_25_out, Opcode3);
  not not_26 (not_26_out, Opcode2);
  not not_27 (not_27_out, Opcode3);
  not not_28 (not_28_out, Opcode1);
  not not_29 (not_29_out, Opcode0);
  not not_30 (not_30_out, Opcode2);
  not not_31 (not_31_out, Opcode1);
  not not_32 (not_32_out, Opcode0);
  not not_33 (not_33_out, Opcode2);
  not not_34 (not_34_out, Opcode1);
  not not_35 (not_35_out, Subop);
  not not_36 (not_36_out, Opcode3);
  not not_37 (not_37_out, Subop);
  not not_38 (not_38_out, Opcode2);
  not not_39 (not_39_out, Subop);
  not not_40 (not_40_out, Opcode2);
  not not_41 (not_41_out, Opcode3);
  not not_42 (not_42_out, Opcode2);
  not not_43 (not_43_out, Opcode1);
  not not_44 (not_44_out, Opcode2);
  not not_45 (not_45_out, Opcode1);
  and and_1 (MemWrite, not_1_out, Opcode2, Opcode1, Opcode0, Subop);
  and and_2 (and_2_out, Opcode3, not_2_out, not_3_out, Opcode0, not_4_out);
  and and_3 (and_3_out, Opcode3, not_5_out, Opcode1, not_6_out);
  and and_4 (Mul_Div, not_7_out, not_8_out, Opcode1, Opcode0);
  and and_5 (and_5_out, not_9_out, Opcode2, not_10_out, Opcode0);
  and and_6 (and_6_out, not_11_out, Opcode2, Opcode1, not_12_out);
  and and_7 (and_7_out, Opcode3, not_13_out, Opcode0, not_14_out);
  and and_8 (and_8_out, not_15_out, Opcode1, Opcode0);
  and and_9 (and_9_out, not_16_out, Opcode2, Opcode1, Subop);
  and and_10 (and_10_out, Opcode3, not_17_out, Opcode0, not_18_out);
  and and_11 (and_11_out, not_19_out, not_20_out, not_21_out);
  and and_12 (and_12_out, not_22_out, not_23_out, Opcode0);
  and and_13 (and_13_out, Opcode1, not_24_out);
  and and_14 (and_14_out, Opcode1, Subop);
  and and_15 (and_15_out, Opcode2, Opcode1);
  and and_16 (and_16_out, not_25_out, not_26_out);
  and and_17 (and_17_out, not_27_out, not_28_out, not_29_out);
  and and_18 (and_18_out, not_30_out, not_31_out, not_32_out);
  and and_19 (and_19_out, not_33_out, not_34_out, not_35_out);
  and and_20 (and_20_out, not_36_out, Opcode1, Opcode0, not_37_out);
  and and_21 (SetDisplay, Opcode3, not_38_out, Opcode1, Opcode0, not_39_out);
  and and_22 (Halt, Opcode3, not_40_out, Opcode1, Opcode0, Subop);
  and and_23 (ALUsrc, not_41_out, not_42_out, not_43_out, Opcode0);
  and and_24 (JumpReg, Opcode3, not_44_out, not_45_out, Opcode0, Subop);
  or or_1 (JumpImmed, and_2_out, and_3_out);
  or or_2 (branch, and_5_out, and_6_out);
  or or_3 (WriteSource_2, Opcode2, and_7_out);
  or or_4 (WriteSource_1, and_8_out, and_9_out, and_10_out);
  or or_5 (WriteSource0, and_11_out, and_12_out, and_13_out, and_14_out, and_15_out);
  or or_6 (RegWrite, and_16_out, and_17_out, and_18_out, and_19_out, and_20_out);
endmodule

module LittleAndGate (
  input  input1,
  input  input2,
  output \output 
);

  and and_1 (\output , input1, input2);
endmodule

module branch_comparator (
  input  Opcode1,
  input  Opcode0,
  input  Subop,
  input  branch,
  input  [15:0] rs,
  output \output 
);

  wire and_1_out, and_2_out, and_3_out, and_4_out, comparator_1_eq, comparator_1_gt, comparator_1_lt,
       comparator_control_1_bn, comparator_control_1_bp, comparator_control_1_bx, comparator_control_1_bz,
       not_1_out, or_1_out, or_2_out, or_3_out;

  Comparator #(.width(16)) comparator_1 (
    .a(rs), .b({16{1'b0}}), .gt(comparator_1_gt), .eq(comparator_1_eq), .lt(comparator_1_lt));
  comparator_control comparator_control_1 (
    .Opcode1(Opcode1), .Opcode0(Opcode0), .Subop(Subop), .bx(comparator_control_1_bx),
    .bz(comparator_control_1_bz), .bp(comparator_control_1_bp), .bn(comparator_control_1_bn));
  not not_1 (not_1_out, comparator_1_eq);
  and and_1 (and_1_out, comparator_1_gt, comparator_control_1_bp);
  and and_2 (and_2_out, comparator_1_eq, comparator_control_1_bz);
  and and_3 (and_3_out, not_1_out, comparator_control_1_bx);
  and and_4 (and_4_out, comparator_1_lt, comparator_control_1_bn);
  or or_1 (or_1_out, and_1_out, and_2_out);
  or or_2 (or_2_out, or_1_out, or_3_out);
  or or_3 (or_3_out, and_3_out, and_4_out);
  and and_5 (\output , branch, or_2_out);
endmodule

module comparator_control (
  input  Opcode1,
  input  Opcode0,
  input  Subop,
  output bx,
  output bz,
  output bp,
  output bn
);

  wire not_1_out, not_2_out, not_3_out, not_4_out, not_5_out, not_6_out;

  not not_1 (not_1_out, Opcode1);
  not not_2 (not_2_out, Subop);
  not not_3 (not_3_out, Opcode1);
  not not_4 (not_4_out, Opcode0);
  not not_5 (not_5_out, Subop);
  not not_6 (not_6_out, Opcode0);
  and and_1 (bx, not_1_out, not_2_out);
  and and_2 (bz, not_3_out, Subop);
  and and_3 (bp, not_4_out, not_5_out);
  and and_4 (bn, not_6_out, Subop);
endmodule
